// Logisim project 2 X 1 MUX.circ as structural Verilog: 2 circuits, main circuit main
module main (
  input  in_1,
  input  in_2,
  input  in_3,
  output out_4
);

  wire and_1_out, and_2_out, not_1_out;

  not not_1 (not_1_out, in_2);
  and and_1 (and_1_out, in_1, not_1_out);
  and and_2 (and_2_out, in_2, in_3);
  or or_1 (out_4, and_1_out, and_2_out);
endmodule

module _4x1_mux (
  input  in_1,
  input  in_2,
  input  in_3,
  input  in_4,
  input  in_5,
  input  in_6,
  output out_7
);

  wire main_1_out_4, main_2_out_4;

  main main_1 (.in_1(in_1), .in_2(in_3), .in_3(in_2), .out_4(main_1_out_4));
  main main_2 (.in_1(in_5), .in_2(in_3), .in_3(in_6), .out_4(main_2_out_4));
  main main_3 (.in_1(main_1_out_4), .in_2(in_4), .in_3(main_2_out_4), .out_4(out_7));
endmodule
