// Logisim project 4 x 1mux.circ as structural Verilog: 3 circuits, main circuit main
module main (
  input  in_1,
  input  in_2,
  input  in_3,
  input  in_4,
  input  in_5,
  input  in_6,
  output out_7,
  output out_8,
  output out_9
);

  _2_X_1_mux u_2_x_1_mux_1 (.in_1(in_1), .in_2(in_3), .in_3(in_2), .out_4(out_7));
  _2_X_1_mux u_2_x_1_mux_2 (.in_1(in_5), .in_2(in_3), .in_3(in_6), .out_4(out_9));
  _2_X_1_mux u_2_x_1_mux_3 (.in_1(out_7), .in_2(in_4), .in_3(out_9), .out_4(out_8));
endmodule

module _2_X_1_mux (
  input  in_1,
  input  in_2,
  input  in_3,
  output out_4
);

  wire and_1_out, and_2_out, not_1_out;

  not not_1 (not_1_out, in_2);
  and and_1 (and_1_out, in_1, not_1_out);
  and and_2 (and_2_out, in_2, in_3);
  or or_1 (out_4, and_1_out, and_2_out);
endmodule

module _8_x_1_Mux (
  input  a0,
  input  a1,
  input  a2,
  input  S1,
  input  a3,
  input  a4,
  input  a5,
  input  a6,
  input  S3,
  input  a7,
  input  S2,
  output O_P
);

  wire n2_x_1_mux_1_out_4, n2_x_1_mux_2_out_4, n2_x_1_mux_3_out_4, n2_x_1_mux_4_out_4, n2_x_1_mux_5_out_4,
       n2_x_1_mux_6_out_4;

  _2_X_1_mux u_2_x_1_mux_1 (.in_1(a0), .in_2(S3), .in_3(a1), .out_4(n2_x_1_mux_1_out_4));
  _2_X_1_mux u_2_x_1_mux_2 (.in_1(a2), .in_2(S3), .in_3(a3), .out_4(n2_x_1_mux_2_out_4));
  _2_X_1_mux u_2_x_1_mux_3 (.in_1(a4), .in_2(S3), .in_3(a5), .out_4(n2_x_1_mux_3_out_4));
  _2_X_1_mux u_2_x_1_mux_4 (.in_1(a6), .in_2(S3), .in_3(a7), .out_4(n2_x_1_mux_4_out_4));
  _2_X_1_mux u_2_x_1_mux_5 (
    .in_1(n2_x_1_mux_1_out_4), .in_2(S2), .in_3(n2_x_1_mux_2_out_4), .out_4(n2_x_1_mux_5_out_4));
  _2_X_1_mux u_2_x_1_mux_6 (
    .in_1(n2_x_1_mux_3_out_4), .in_2(S2), .in_3(n2_x_1_mux_4_out_4), .out_4(n2_x_1_mux_6_out_4));
  _2_X_1_mux u_2_x_1_mux_7 (.in_1(n2_x_1_mux_5_out_4), .in_2(S1), .in_3(n2_x_1_mux_6_out_4), .out_4(O_P));
endmodule
