// Logisim project 8 BIT AND.circ as structural Verilog
module _8_bit_AND (
  input  in_1,
  input  in_2,
  input  in_3,
  input  in_4,
  input  in_5,
  input  in_6,
  input  in_7,
  input  in_8,
  input  in_9,
  input  in_10,
  input  in_11,
  input  in_12,
  input  in_13,
  input  in_14,
  input  in_15,
  input  in_16,
  output out_17,
  output out_18,
  output out_19,
  output out_20,
  output out_21,
  output out_22,
  output out_23,
  output out_24
);

  and and_1 (out_17, in_1, in_2);
  and and_2 (out_18, in_3, in_4);
  and and_3 (out_19, in_5, in_6);
  and and_4 (out_20, in_7, in_8);
  and and_5 (out_21, in_9, in_10);
  and and_6 (out_22, in_11, in_12);
  and and_7 (out_23, in_13, in_14);
  and and_8 (out_24, in_15, in_16);
endmodule

module _8_BIT_OR (
  input  in_1,
  input  in_2,
  input  in_3,
  input  in_4,
  input  in_5,
  input  in_6,
  input  in_7,
  input  in_8,
  input  in_9,
  input  in_10,
  input  in_11,
  input  in_12,
  input  in_13,
  input  in_14,
  input  in_15,
  input  in_16,
  output out_17,
  output out_18,
  output out_19,
  output out_20,
  output out_21,
  output out_22,
  output out_23,
  output out_24
);

  or or_1 (out_17, in_1, in_2);
  or or_2 (out_18, in_3, in_4);
  or or_3 (out_19, in_5, in_6);
  or or_4 (out_20, in_7, in_8);
  or or_5 (out_21, in_9, in_10);
  or or_6 (out_22, in_11, in_12);
  or or_7 (out_23, in_13, in_14);
  or or_8 (out_24, in_15, in_16);
endmodule

module _8_BIT_NOT (
  input  in_1,
  input  in_2,
  input  in_3,
  input  in_4,
  input  in_5,
  input  in_6,
  input  in_7,
  input  in_8,
  output out_9,
  output out_10,
  output out_11,
  output out_12,
  output out_13,
  output out_14,
  output out_15,
  output out_16
);

  not not_1 (out_9, in_1);
  not not_2 (out_10, in_2);
  not not_3 (out_11, in_3);
  not not_4 (out_12, in_4);
  not not_5 (out_13, in_5);
  not not_6 (out_14, in_6);
  not not_7 (out_15, in_7);
  not not_8 (out_16, in_8);
endmodule
