// Logisim project CLA.circ as structural Verilog: 7 circuits, main circuit main
module main (
  input  [31:0] in_1,
  input  [31:0] in_2,
  input  SELECTOR,
  output [31:0] OUTPUT,
  output CARRY
);

  wire [31:0] chose_negate_1_out_3;

  ADDER_CLA adder_cla_1 (.A(in_1), .B(chose_negate_1_out_3), .Cin(SELECTOR), .Cout(CARRY), .OUT(OUTPUT));
  CHOSE_NEGATE chose_negate_1 (.in_2(SELECTOR), .out_3(chose_negate_1_out_3), .INPUT(in_2));
endmodule

module CARRY_GEN (
  input  [7:0] A,
  input  [7:0] B,
  input  C0,
  output [7:0] OUTPUT
);

  wire and_1_out, and_2_out, and_3_out, and_4_out, and_5_out, and_6_out, and_7_out, and_8_out, and_9_out,
       and_10_out, and_11_out, and_12_out, and_13_out, and_14_out, and_15_out, G0_out, P0_out, xor_1_out,
       xor_2_out, xor_3_out, xor_4_out, xor_5_out, xor_6_out, xor_7_out;

  xor P0 (P0_out, A[0], B[0]);
  and G0 (G0_out, A[0], B[0]);
  xor xor_1 (xor_1_out, A[1], B[1]);
  and and_1 (and_1_out, A[1], B[1]);
  xor xor_2 (xor_2_out, A[2], B[2]);
  and and_2 (and_2_out, A[2], B[2]);
  xor xor_3 (xor_3_out, A[3], B[3]);
  and and_3 (and_3_out, A[3], B[3]);
  xor xor_4 (xor_4_out, A[4], B[4]);
  and and_4 (and_4_out, A[4], B[4]);
  xor xor_5 (xor_5_out, A[5], B[5]);
  and and_5 (and_5_out, A[5], B[5]);
  xor xor_6 (xor_6_out, A[6], B[6]);
  and and_6 (and_6_out, A[6], B[6]);
  xor xor_7 (xor_7_out, A[7], B[7]);
  and and_7 (and_7_out, A[7], B[7]);
  and and_8 (and_8_out, C0, P0_out);
  and and_9 (and_9_out, OUTPUT[3], xor_4_out);
  or or_1 (OUTPUT[0], and_8_out, G0_out);
  and and_10 (and_10_out, OUTPUT[0], xor_1_out);
  and and_11 (and_11_out, OUTPUT[1], xor_2_out);
  and and_12 (and_12_out, OUTPUT[2], xor_3_out);
  and and_13 (and_13_out, OUTPUT[4], xor_5_out);
  and and_14 (and_14_out, OUTPUT[5], xor_6_out);
  and and_15 (and_15_out, OUTPUT[6], xor_7_out);
  or or_2 (OUTPUT[1], and_10_out, and_1_out);
  or or_3 (OUTPUT[2], and_11_out, and_2_out);
  or or_4 (OUTPUT[3], and_12_out, and_3_out);
  or or_5 (OUTPUT[4], and_9_out, and_4_out);
  or or_6 (OUTPUT[5], and_13_out, and_5_out);
  or or_7 (OUTPUT[6], and_14_out, and_6_out);
  or or_8 (OUTPUT[7], and_15_out, and_7_out);
endmodule

module ADDER (
  input  A_in,
  input  B_in,
  input  C,
  output SUM
);

  wire xor_1_out;

  xor xor_1 (xor_1_out, A_in, B_in);
  xor xor_2 (SUM, xor_1_out, C);
endmodule

module _8_BIT_CLA (
  input  in_1,
  input  [7:0] A,
  input  [7:0] B,
  output Cout,
  output [7:0] _8BIT_sum
);

  wire [6:0] carry_gen_1_output;

  CARRY_GEN carry_gen_1 (.A(A), .B(B), .C0(in_1), .OUTPUT({Cout, carry_gen_1_output}));
  ADDER adder_1 (.A_in(A[0]), .B_in(B[0]), .C(in_1), .SUM(_8BIT_sum[0]));
  ADDER adder_2 (.A_in(A[2]), .B_in(B[2]), .C(carry_gen_1_output[1]), .SUM(_8BIT_sum[2]));
  ADDER adder_3 (.A_in(A[1]), .B_in(B[1]), .C(carry_gen_1_output[0]), .SUM(_8BIT_sum[1]));
  ADDER adder_4 (.A_in(A[4]), .B_in(B[4]), .C(carry_gen_1_output[3]), .SUM(_8BIT_sum[4]));
  ADDER adder_5 (.A_in(A[3]), .B_in(B[3]), .C(carry_gen_1_output[2]), .SUM(_8BIT_sum[3]));
  ADDER adder_6 (.A_in(A[5]), .B_in(B[5]), .C(carry_gen_1_output[4]), .SUM(_8BIT_sum[5]));
  ADDER adder_7 (.A_in(A[6]), .B_in(B[6]), .C(carry_gen_1_output[5]), .SUM(_8BIT_sum[6]));
  ADDER adder_8 (.A_in(A[7]), .B_in(B[7]), .C(carry_gen_1_output[6]), .SUM(_8BIT_sum[7]));
endmodule

module ADDER_CLA (
  input  Cin,
  input  [31:0] A,
  input  [31:0] B,
  output [31:0] OUT,
  output Cout
);

  wire n8_bit_cla_2_cout, n8_bit_cla_3_cout, n8_bit_cla_4_cout;

  _8_BIT_CLA u_8_bit_cla_1 (.A(B[31:24]), .B(A[31:24]), .in_1(n8_bit_cla_2_cout), .Cout(Cout), ._8BIT_sum(OUT[31:24]));
  _8_BIT_CLA u_8_bit_cla_2 (
    .A(B[23:16]), .B(A[23:16]), .in_1(n8_bit_cla_3_cout), .Cout(n8_bit_cla_2_cout), ._8BIT_sum(OUT[23:16]));
  _8_BIT_CLA u_8_bit_cla_3 (
    .A(B[15:8]), .B(A[15:8]), .in_1(n8_bit_cla_4_cout), .Cout(n8_bit_cla_3_cout), ._8BIT_sum(OUT[15:8]));
  _8_BIT_CLA u_8_bit_cla_4 (.A(B[7:0]), .B(A[7:0]), .in_1(Cin), .Cout(n8_bit_cla_4_cout), ._8BIT_sum(OUT[7:0]));
endmodule

module CHOSE_NEGATE (
  input  [31:0] INPUT,
  input  in_2,
  output [31:0] out_3
);

  wire not_1_out, not_2_out, not_3_out, not_4_out, not_5_out, not_6_out, not_7_out, not_8_out, not_9_out,
       not_10_out, not_11_out, not_12_out, not_13_out, not_14_out, not_15_out, not_16_out, not_17_out,
       not_18_out, not_19_out, not_20_out, not_21_out, not_22_out, not_23_out, not_24_out, not_25_out,
       not_26_out, not_27_out, not_28_out, not_29_out, not_30_out, not_31_out, not_32_out;

  not not_1 (not_1_out, INPUT[31]);
  _2_1_MUX u_2_1_mux_1 (.in_1(INPUT[31]), .in_2(not_1_out), .in_3(in_2), .out_4(out_3[31]));
  not not_2 (not_2_out, INPUT[30]);
  _2_1_MUX u_2_1_mux_2 (.in_1(INPUT[30]), .in_2(not_2_out), .in_3(in_2), .out_4(out_3[30]));
  not not_3 (not_3_out, INPUT[29]);
  _2_1_MUX u_2_1_mux_3 (.in_1(INPUT[29]), .in_2(not_3_out), .in_3(in_2), .out_4(out_3[29]));
  not not_4 (not_4_out, INPUT[28]);
  _2_1_MUX u_2_1_mux_4 (.in_1(INPUT[28]), .in_2(not_4_out), .in_3(in_2), .out_4(out_3[28]));
  not not_5 (not_5_out, INPUT[27]);
  _2_1_MUX u_2_1_mux_5 (.in_1(INPUT[27]), .in_2(not_5_out), .in_3(in_2), .out_4(out_3[27]));
  not not_6 (not_6_out, INPUT[26]);
  _2_1_MUX u_2_1_mux_6 (.in_1(INPUT[26]), .in_2(not_6_out), .in_3(in_2), .out_4(out_3[26]));
  not not_7 (not_7_out, INPUT[25]);
  _2_1_MUX u_2_1_mux_7 (.in_1(INPUT[25]), .in_2(not_7_out), .in_3(in_2), .out_4(out_3[25]));
  not not_8 (not_8_out, INPUT[24]);
  _2_1_MUX u_2_1_mux_8 (.in_1(INPUT[24]), .in_2(not_8_out), .in_3(in_2), .out_4(out_3[24]));
  not not_9 (not_9_out, INPUT[23]);
  _2_1_MUX u_2_1_mux_9 (.in_1(INPUT[23]), .in_2(not_9_out), .in_3(in_2), .out_4(out_3[23]));
  not not_10 (not_10_out, INPUT[22]);
  _2_1_MUX u_2_1_mux_10 (.in_1(INPUT[22]), .in_2(not_10_out), .in_3(in_2), .out_4(out_3[22]));
  not not_11 (not_11_out, INPUT[21]);
  _2_1_MUX u_2_1_mux_11 (.in_1(INPUT[21]), .in_2(not_11_out), .in_3(in_2), .out_4(out_3[21]));
  not not_12 (not_12_out, INPUT[20]);
  _2_1_MUX u_2_1_mux_12 (.in_1(INPUT[20]), .in_2(not_12_out), .in_3(in_2), .out_4(out_3[20]));
  not not_13 (not_13_out, INPUT[19]);
  _2_1_MUX u_2_1_mux_13 (.in_1(INPUT[19]), .in_2(not_13_out), .in_3(in_2), .out_4(out_3[19]));
  not not_14 (not_14_out, INPUT[18]);
  _2_1_MUX u_2_1_mux_14 (.in_1(INPUT[18]), .in_2(not_14_out), .in_3(in_2), .out_4(out_3[18]));
  not not_15 (not_15_out, INPUT[17]);
  _2_1_MUX u_2_1_mux_15 (.in_1(INPUT[17]), .in_2(not_15_out), .in_3(in_2), .out_4(out_3[17]));
  not not_16 (not_16_out, INPUT[16]);
  _2_1_MUX u_2_1_mux_16 (.in_1(INPUT[16]), .in_2(not_16_out), .in_3(in_2), .out_4(out_3[16]));
  not not_17 (not_17_out, INPUT[15]);
  _2_1_MUX u_2_1_mux_17 (.in_1(INPUT[15]), .in_2(not_17_out), .in_3(in_2), .out_4(out_3[15]));
  not not_18 (not_18_out, INPUT[14]);
  _2_1_MUX u_2_1_mux_18 (.in_1(INPUT[14]), .in_2(not_18_out), .in_3(in_2), .out_4(out_3[14]));
  not not_19 (not_19_out, INPUT[13]);
  _2_1_MUX u_2_1_mux_19 (.in_1(INPUT[13]), .in_2(not_19_out), .in_3(in_2), .out_4(out_3[13]));
  not not_20 (not_20_out, INPUT[12]);
  _2_1_MUX u_2_1_mux_20 (.in_1(INPUT[12]), .in_2(not_20_out), .in_3(in_2), .out_4(out_3[12]));
  not not_21 (not_21_out, INPUT[11]);
  _2_1_MUX u_2_1_mux_21 (.in_1(INPUT[11]), .in_2(not_21_out), .in_3(in_2), .out_4(out_3[11]));
  not not_22 (not_22_out, INPUT[10]);
  _2_1_MUX u_2_1_mux_22 (.in_1(INPUT[10]), .in_2(not_22_out), .in_3(in_2), .out_4(out_3[10]));
  not not_23 (not_23_out, INPUT[9]);
  _2_1_MUX u_2_1_mux_23 (.in_1(INPUT[9]), .in_2(not_23_out), .in_3(in_2), .out_4(out_3[9]));
  not not_24 (not_24_out, INPUT[8]);
  _2_1_MUX u_2_1_mux_24 (.in_1(INPUT[8]), .in_2(not_24_out), .in_3(in_2), .out_4(out_3[8]));
  not not_25 (not_25_out, INPUT[7]);
  _2_1_MUX u_2_1_mux_25 (.in_1(INPUT[7]), .in_2(not_25_out), .in_3(in_2), .out_4(out_3[7]));
  not not_26 (not_26_out, INPUT[6]);
  _2_1_MUX u_2_1_mux_26 (.in_1(INPUT[6]), .in_2(not_26_out), .in_3(in_2), .out_4(out_3[6]));
  not not_27 (not_27_out, INPUT[5]);
  _2_1_MUX u_2_1_mux_27 (.in_1(INPUT[5]), .in_2(not_27_out), .in_3(in_2), .out_4(out_3[5]));
  not not_28 (not_28_out, INPUT[4]);
  _2_1_MUX u_2_1_mux_28 (.in_1(INPUT[4]), .in_2(not_28_out), .in_3(in_2), .out_4(out_3[4]));
  not not_29 (not_29_out, INPUT[3]);
  _2_1_MUX u_2_1_mux_29 (.in_1(INPUT[3]), .in_2(not_29_out), .in_3(in_2), .out_4(out_3[3]));
  not not_30 (not_30_out, INPUT[2]);
  _2_1_MUX u_2_1_mux_30 (.in_1(INPUT[2]), .in_2(not_30_out), .in_3(in_2), .out_4(out_3[2]));
  not not_31 (not_31_out, INPUT[1]);
  _2_1_MUX u_2_1_mux_31 (.in_1(INPUT[1]), .in_2(not_31_out), .in_3(in_2), .out_4(out_3[1]));
  not not_32 (not_32_out, INPUT[0]);
  _2_1_MUX u_2_1_mux_32 (.in_1(INPUT[0]), .in_2(not_32_out), .in_3(in_2), .out_4(out_3[0]));
endmodule

module _2_1_MUX (
  input  in_1,
  input  in_2,
  input  in_3,
  output out_4
);

  wire and_1_out, and_2_out, not_1_out;

  and and_1 (and_1_out, in_2, in_3);
  not not_1 (not_1_out, in_3);
  and and_2 (and_2_out, in_1, not_1_out);
  or or_1 (out_4, and_2_out, and_1_out);
endmodule
