// Logisim project EX2.circ as structural Verilog
module _8_bit_AND (
  input  A1,
  input  B1,
  input  A2,
  input  B2,
  input  A3,
  input  B3,
  input  A4,
  input  B4,
  input  A5,
  input  B5,
  input  A6,
  input  B6,
  input  A7,
  input  B7,
  input  A8,
  input  B8,
  output out_17,
  output out_18,
  output out_19,
  output out_20,
  output out_21,
  output out_22,
  output out_23,
  output out_24
);

  and and_1 (out_17, A1, B1);
  and and_2 (out_18, A2, B2);
  and and_3 (out_19, A3, B3);
  and and_4 (out_20, A4, B4);
  and and_5 (out_21, A5, B5);
  and and_6 (out_22, A6, B6);
  and and_7 (out_23, A7, B7);
  and and_8 (out_24, A8, B8);
endmodule

module _8_BIT_OR (
  input  A1,
  input  B1,
  input  A2,
  input  B2,
  input  A3,
  input  B3,
  input  A4,
  input  B4,
  input  A5,
  input  B5,
  input  A6,
  input  B6,
  input  A7,
  input  B7,
  input  A8,
  input  B8,
  output out_17,
  output out_18,
  output out_19,
  output out_20,
  output out_21,
  output out_22,
  output out_23,
  output out_24
);

  or or_1 (out_17, A1, B1);
  or or_2 (out_18, A2, B2);
  or or_3 (out_19, A3, B3);
  or or_4 (out_20, A4, B4);
  or or_5 (out_21, A5, B5);
  or or_6 (out_22, A6, B6);
  or or_7 (out_23, A7, B7);
  or or_8 (out_24, A8, B8);
endmodule

module _8_BIT_NOT (
  input  in_1,
  input  in_2,
  input  in_3,
  input  in_4,
  input  in_5,
  input  in_6,
  input  in_7,
  input  in_8,
  output out_9,
  output out_10,
  output out_11,
  output out_12,
  output out_13,
  output out_14,
  output out_15,
  output out_16
);

  not not_1 (out_9, in_1);
  not not_2 (out_10, in_2);
  not not_3 (out_11, in_3);
  not not_4 (out_12, in_4);
  not not_5 (out_13, in_5);
  not not_6 (out_14, in_6);
  not not_7 (out_15, in_7);
  not not_8 (out_16, in_8);
endmodule

module _8_BIT_EXOR (
  input  A1,
  input  B1,
  input  A2,
  input  B2,
  input  A3,
  input  B3,
  input  A4,
  input  B4,
  input  A5,
  input  B5,
  input  A6,
  input  B6,
  input  A7,
  input  B7,
  input  A8,
  input  B8,
  output out_17,
  output out_18,
  output out_19,
  output out_20,
  output out_21,
  output out_22,
  output out_23,
  output out_24
);

  xor xor_1 (out_17, A1, B1);
  xor xor_2 (out_18, A2, B2);
  xor xor_3 (out_19, A3, B3);
  xor xor_4 (out_20, A4, B4);
  xor xor_5 (out_21, A5, B5);
  xor xor_6 (out_22, A6, B6);
  xor xor_7 (out_23, A7, B7);
  xor xor_8 (out_24, A8, B8);
endmodule

module tristate (
  input  A1,
  input  A1_2,
  input  B1,
  input  B1_2,
  input  A2,
  input  A2_2,
  input  B2,
  input  B2_2,
  input  A3,
  input  A3_2,
  input  B3,
  input  B3_2,
  input  A4,
  input  A4_2,
  input  B4,
  input  B4_2,
  input  A5,
  input  A5_2,
  input  B5,
  input  B5_2,
  input  A6,
  input  A6_2,
  input  B6,
  input  B6_2,
  input  A7,
  input  in_26,
  input  A7_2,
  input  in_28,
  input  B7,
  input  B7_2,
  input  A8,
  input  A8_2,
  input  B8,
  input  B8_2,
  input  A1_3,
  input  B1_3,
  input  in_37,
  input  A2_3,
  input  in_39,
  input  B2_3,
  input  in_41,
  input  A3_3,
  input  in_43,
  input  B3_3,
  input  in_45,
  input  A4_3,
  input  in_47,
  input  B4_3,
  input  in_49,
  input  A5_3,
  input  in_51,
  input  B5_3,
  input  A6_3,
  input  in_54,
  input  B6_3,
  input  A7_3,
  input  in_57,
  input  B7_3,
  input  A8_3,
  input  B8_3,
  output out_61,
  output out_62,
  output out_63,
  output out_64,
  output out_65,
  output out_66,
  output out_67,
  output out_68,
  output out_69,
  output out_70,
  output out_71,
  output out_72,
  output out_73,
  output out_74,
  output out_75,
  output out_76,
  output out_77,
  output out_78,
  output out_79,
  output out_80,
  output out_81,
  output out_82,
  output out_83,
  output out_84,
  output out_85,
  output out_86,
  output out_87,
  output out_88,
  output out_89,
  output out_90,
  output out_91,
  output out_92
);

  wire n8_bit_and_1_out_17, n8_bit_and_1_out_18, n8_bit_and_1_out_19, n8_bit_and_1_out_20,
       n8_bit_and_1_out_21, n8_bit_and_1_out_22, n8_bit_and_1_out_23, n8_bit_and_1_out_24,
       n8_bit_exor_1_out_17, n8_bit_exor_1_out_18, n8_bit_exor_1_out_19, n8_bit_exor_1_out_20,
       n8_bit_exor_1_out_21, n8_bit_exor_1_out_22, n8_bit_exor_1_out_23, n8_bit_exor_1_out_24,
       n8_bit_not_1_out_9, n8_bit_not_1_out_10, n8_bit_not_1_out_11, n8_bit_not_1_out_12,
       n8_bit_not_1_out_13, n8_bit_not_1_out_14, n8_bit_not_1_out_15, n8_bit_not_1_out_16,
       n8_bit_or_1_out_17, n8_bit_or_1_out_18, n8_bit_or_1_out_19, n8_bit_or_1_out_20, n8_bit_or_1_out_21,
       n8_bit_or_1_out_22, n8_bit_or_1_out_23, n8_bit_or_1_out_24;

  _8_bit_AND u_8_bit_and_1 (
    .A1(A1), .B1(B1), .A2(A2), .B2(B2), .A3(A3), .B3(B3), .A4(A4), .B4(B4), .A5(A5), .B5(B5), .A6(A6),
    .B6(B6), .A7(A7), .B7(B7), .A8(A8), .B8(B8), .out_17(n8_bit_and_1_out_17), .out_18(n8_bit_and_1_out_18),
    .out_19(n8_bit_and_1_out_19), .out_20(n8_bit_and_1_out_20), .out_21(n8_bit_and_1_out_21),
    .out_22(n8_bit_and_1_out_22), .out_23(n8_bit_and_1_out_23), .out_24(n8_bit_and_1_out_24));
  assign out_61 = in_26 ? n8_bit_and_1_out_17 : 1'bz;  // Controlled_Buffer controlled_buffer_1
  assign out_63 = in_26 ? n8_bit_and_1_out_18 : 1'bz;  // Controlled_Buffer controlled_buffer_2
  assign out_65 = in_26 ? n8_bit_and_1_out_19 : 1'bz;  // Controlled_Buffer controlled_buffer_3
  assign out_67 = in_26 ? n8_bit_and_1_out_20 : 1'bz;  // Controlled_Buffer controlled_buffer_4
  assign out_69 = in_26 ? n8_bit_and_1_out_21 : 1'bz;  // Controlled_Buffer controlled_buffer_5
  assign out_71 = in_26 ? n8_bit_and_1_out_22 : 1'bz;  // Controlled_Buffer controlled_buffer_6
  assign out_73 = in_26 ? n8_bit_and_1_out_23 : 1'bz;  // Controlled_Buffer controlled_buffer_7
  assign out_75 = in_26 ? n8_bit_and_1_out_24 : 1'bz;  // Controlled_Buffer controlled_buffer_8
  _8_BIT_EXOR u_8_bit_exor_1 (
    .A1(A1_3), .B1(B1_3), .A2(A2_3), .B2(B2_3), .A3(A3_3), .B3(B3_3), .A4(A4_3), .B4(B4_3), .A5(A5_3),
    .B5(B5_3), .A6(A6_3), .B6(B6_3), .A7(A7_3), .B7(B7_3), .A8(A8_3), .B8(B8_3),
    .out_17(n8_bit_exor_1_out_17), .out_18(n8_bit_exor_1_out_18), .out_19(n8_bit_exor_1_out_19),
    .out_20(n8_bit_exor_1_out_20), .out_21(n8_bit_exor_1_out_21), .out_22(n8_bit_exor_1_out_22),
    .out_23(n8_bit_exor_1_out_23), .out_24(n8_bit_exor_1_out_24));
  assign out_77 = in_57 ? n8_bit_exor_1_out_17 : 1'bz;  // Controlled_Buffer controlled_buffer_9
  assign out_78 = in_57 ? n8_bit_exor_1_out_18 : 1'bz;  // Controlled_Buffer controlled_buffer_10
  assign out_80 = in_57 ? n8_bit_exor_1_out_19 : 1'bz;  // Controlled_Buffer controlled_buffer_11
  assign out_82 = in_57 ? n8_bit_exor_1_out_20 : 1'bz;  // Controlled_Buffer controlled_buffer_12
  assign out_84 = in_57 ? n8_bit_exor_1_out_21 : 1'bz;  // Controlled_Buffer controlled_buffer_13
  assign out_87 = in_57 ? n8_bit_exor_1_out_22 : 1'bz;  // Controlled_Buffer controlled_buffer_14
  assign out_89 = in_57 ? n8_bit_exor_1_out_23 : 1'bz;  // Controlled_Buffer controlled_buffer_15
  assign out_92 = in_57 ? n8_bit_exor_1_out_24 : 1'bz;  // Controlled_Buffer controlled_buffer_16
  _8_BIT_OR u_8_bit_or_1 (
    .A1(A1_2), .B1(B1_2), .A2(A2_2), .B2(B2_2), .A3(A3_2), .B3(B3_2), .A4(A4_2), .B4(B4_2), .A5(A5_2),
    .B5(B5_2), .A6(A6_2), .B6(B6_2), .A7(A7_2), .B7(B7_2), .A8(A8_2), .B8(B8_2), .out_17(n8_bit_or_1_out_17),
    .out_18(n8_bit_or_1_out_18), .out_19(n8_bit_or_1_out_19), .out_20(n8_bit_or_1_out_20),
    .out_21(n8_bit_or_1_out_21), .out_22(n8_bit_or_1_out_22), .out_23(n8_bit_or_1_out_23),
    .out_24(n8_bit_or_1_out_24));
  _8_BIT_NOT u_8_bit_not_1 (
    .in_1(in_37), .in_2(in_39), .in_3(in_41), .in_4(in_43), .in_5(in_45), .in_6(in_47), .in_7(in_49),
    .in_8(in_51), .out_9(n8_bit_not_1_out_9), .out_10(n8_bit_not_1_out_10), .out_11(n8_bit_not_1_out_11),
    .out_12(n8_bit_not_1_out_12), .out_13(n8_bit_not_1_out_13), .out_14(n8_bit_not_1_out_14),
    .out_15(n8_bit_not_1_out_15), .out_16(n8_bit_not_1_out_16));
  assign out_62 = in_28 ? n8_bit_or_1_out_17 : 1'bz;  // Controlled_Buffer controlled_buffer_17
  assign out_64 = in_28 ? n8_bit_or_1_out_18 : 1'bz;  // Controlled_Buffer controlled_buffer_18
  assign out_66 = in_28 ? n8_bit_or_1_out_19 : 1'bz;  // Controlled_Buffer controlled_buffer_19
  assign out_68 = in_28 ? n8_bit_or_1_out_20 : 1'bz;  // Controlled_Buffer controlled_buffer_20
  assign out_70 = in_28 ? n8_bit_or_1_out_21 : 1'bz;  // Controlled_Buffer controlled_buffer_21
  assign out_72 = in_28 ? n8_bit_or_1_out_22 : 1'bz;  // Controlled_Buffer controlled_buffer_22
  assign out_74 = in_28 ? n8_bit_or_1_out_23 : 1'bz;  // Controlled_Buffer controlled_buffer_23
  assign out_76 = in_28 ? n8_bit_or_1_out_24 : 1'bz;  // Controlled_Buffer controlled_buffer_24
  assign out_79 = in_54 ? n8_bit_not_1_out_9 : 1'bz;  // Controlled_Buffer controlled_buffer_25
  assign out_81 = in_54 ? n8_bit_not_1_out_10 : 1'bz;  // Controlled_Buffer controlled_buffer_26
  assign out_83 = in_54 ? n8_bit_not_1_out_11 : 1'bz;  // Controlled_Buffer controlled_buffer_27
  assign out_85 = in_54 ? n8_bit_not_1_out_12 : 1'bz;  // Controlled_Buffer controlled_buffer_28
  assign out_86 = in_54 ? n8_bit_not_1_out_13 : 1'bz;  // Controlled_Buffer controlled_buffer_29
  assign out_88 = in_54 ? n8_bit_not_1_out_14 : 1'bz;  // Controlled_Buffer controlled_buffer_30
  assign out_90 = in_54 ? n8_bit_not_1_out_15 : 1'bz;  // Controlled_Buffer controlled_buffer_31
  assign out_91 = in_54 ? n8_bit_not_1_out_16 : 1'bz;  // Controlled_Buffer controlled_buffer_32
endmodule
