// Logisim project EXercise 5.circ as structural Verilog
module _8_NOT (
  input  A0,
  input  A1,
  input  A2,
  input  A3,
  input  A4,
  input  A5,
  input  A6,
  input  A7,
  input  [2:0] in_9,
  output out_10
);

  wire n8_bit_not_1_p9, n8_bit_not_1_p10, n8_bit_not_1_p11, n8_bit_not_1_p12, n8_bit_not_1_p13,
       n8_bit_not_1_p14, n8_bit_not_1_p15, n8_bit_not_1_p16;

  // _8_BIT_NOT 8_bit_not_1: pin names not known; wires that end beside it: A0, A1, A2, A3, A4, A5, A6, A7, n8_bit_not_1_p9, n8_bit_not_1_p10, n8_bit_not_1_p11, n8_bit_not_1_p12, n8_bit_not_1_p13, n8_bit_not_1_p14, n8_bit_not_1_p15, n8_bit_not_1_p16
  Multiplexer #(.select(3)) multiplexer_1 (
    .in0(n8_bit_not_1_p9), .in1(n8_bit_not_1_p10), .in2(n8_bit_not_1_p11), .in3(n8_bit_not_1_p12),
    .in4(n8_bit_not_1_p13), .in5(n8_bit_not_1_p14), .in6(n8_bit_not_1_p15), .in7(n8_bit_not_1_p16),
    .out(out_10), .sel(in_9));  // open: en
endmodule

module _8_AND (
  input  A0,
  input  B0,
  input  A1,
  input  B1,
  input  A2,
  input  B2,
  input  A3,
  input  B3,
  input  A4,
  input  B4,
  input  A5,
  input  B5,
  input  A6,
  input  B6,
  input  [2:0] in_15,
  input  A7,
  input  B7,
  output out_18
);

  wire n8_bit_o_p_and_1_p17, n8_bit_o_p_and_1_p18, n8_bit_o_p_and_1_p19, n8_bit_o_p_and_1_p20,
       n8_bit_o_p_and_1_p21, n8_bit_o_p_and_1_p22, n8_bit_o_p_and_1_p23, n8_bit_o_p_and_1_p24;

  // _8_BIT_O_P_AND 8_bit_o_p_and_1: pin names not known; wires that end beside it: A0, B0, A1, B1, A2, B2, A3, B3, A4, B4, A5, B5, A6, B6, A7, B7, n8_bit_o_p_and_1_p17, n8_bit_o_p_and_1_p18, n8_bit_o_p_and_1_p19, n8_bit_o_p_and_1_p20, n8_bit_o_p_and_1_p21, n8_bit_o_p_and_1_p22, n8_bit_o_p_and_1_p23, n8_bit_o_p_and_1_p24
  Multiplexer #(.select(3)) multiplexer_1 (
    .in0(n8_bit_o_p_and_1_p17), .in1(n8_bit_o_p_and_1_p18), .in2(n8_bit_o_p_and_1_p19),
    .in3(n8_bit_o_p_and_1_p20), .in4(n8_bit_o_p_and_1_p21), .in5(n8_bit_o_p_and_1_p22),
    .in6(n8_bit_o_p_and_1_p23), .in7(n8_bit_o_p_and_1_p24), .out(out_18), .sel(in_15));  // open: en
endmodule

module _8_OR (
  input  A0,
  input  B0,
  input  A1,
  input  B1,
  input  A2,
  input  B2,
  input  A3,
  input  B3,
  input  A4,
  input  B4,
  input  A5,
  input  B5,
  input  A6,
  input  B6,
  input  A7,
  input  [2:0] in_16,
  input  B7,
  output out_18
);

  wire n8_bit_o_p_or_1_p17, n8_bit_o_p_or_1_p18, n8_bit_o_p_or_1_p19, n8_bit_o_p_or_1_p20,
       n8_bit_o_p_or_1_p21, n8_bit_o_p_or_1_p22, n8_bit_o_p_or_1_p23, n8_bit_o_p_or_1_p24;

  // _8_BIT_O_P_OR 8_bit_o_p_or_1: pin names not known; wires that end beside it: A0, B0, A1, B1, A2, B2, A3, B3, A4, B4, A5, B5, A6, B6, A7, B7, n8_bit_o_p_or_1_p17, n8_bit_o_p_or_1_p18, n8_bit_o_p_or_1_p19, n8_bit_o_p_or_1_p20, n8_bit_o_p_or_1_p21, n8_bit_o_p_or_1_p22, n8_bit_o_p_or_1_p23, n8_bit_o_p_or_1_p24
  Multiplexer #(.select(3)) multiplexer_1 (
    .in0(n8_bit_o_p_or_1_p17), .in1(n8_bit_o_p_or_1_p18), .in2(n8_bit_o_p_or_1_p19),
    .in3(n8_bit_o_p_or_1_p20), .in4(n8_bit_o_p_or_1_p21), .in5(n8_bit_o_p_or_1_p22),
    .in6(n8_bit_o_p_or_1_p23), .in7(n8_bit_o_p_or_1_p24), .out(out_18), .sel(in_16));  // open: en
endmodule

module _8_XOR (
  input  A0,
  input  B0,
  input  A1,
  input  B1,
  input  A2,
  input  B2,
  input  A3,
  input  B3,
  input  A4,
  input  B4,
  input  A5,
  input  B5,
  input  A6,
  input  B6,
  input  A7,
  input  B7,
  input  [2:0] in_17,
  output out_18
);

  wire n8_bit_o_p_xor_1_p17, n8_bit_o_p_xor_1_p18, n8_bit_o_p_xor_1_p19, n8_bit_o_p_xor_1_p20,
       n8_bit_o_p_xor_1_p21, n8_bit_o_p_xor_1_p22, n8_bit_o_p_xor_1_p23, n8_bit_o_p_xor_1_p24;

  // _8_BIT_O_P_XOR 8_bit_o_p_xor_1: pin names not known; wires that end beside it: A0, B0, A1, B1, A2, B2, A3, B3, A4, B4, A5, B5, A6, B6, A7, B7, n8_bit_o_p_xor_1_p17, n8_bit_o_p_xor_1_p18, n8_bit_o_p_xor_1_p19, n8_bit_o_p_xor_1_p20, n8_bit_o_p_xor_1_p21, n8_bit_o_p_xor_1_p22, n8_bit_o_p_xor_1_p23, n8_bit_o_p_xor_1_p24
  Multiplexer #(.select(3)) multiplexer_1 (
    .in0(n8_bit_o_p_xor_1_p17), .in1(n8_bit_o_p_xor_1_p18), .in2(n8_bit_o_p_xor_1_p19),
    .in3(n8_bit_o_p_xor_1_p20), .in4(n8_bit_o_p_xor_1_p21), .in5(n8_bit_o_p_xor_1_p22),
    .in6(n8_bit_o_p_xor_1_p23), .in7(n8_bit_o_p_xor_1_p24), .out(out_18), .sel(in_17));  // open: en
endmodule
