// Logisim project assignment6.circ as structural Verilog: 2 circuits, main circuit main
module main (
  input  x0,
  input  x1,
  input  x2,
  input  x3,
  input  s1,
  input  s0,
  output y0,
  output y1,
  output y2,
  output y3
);

  wire n2_4_decoder_1_out_3, n2_4_decoder_1_out_4, n2_4_decoder_1_out_5, n2_4_decoder_1_out_6;

  _2_4_decoder u_2_4_decoder_1 (
    .in_1(s1), .in_2(s0), .out_3(n2_4_decoder_1_out_3), .out_4(n2_4_decoder_1_out_4),
    .out_5(n2_4_decoder_1_out_5), .out_6(n2_4_decoder_1_out_6));
  assign y0 = n2_4_decoder_1_out_3 ? x0 : 1'bz;  // Controlled_Buffer controlled_buffer_1
  assign y1 = n2_4_decoder_1_out_4 ? x0 : 1'bz;  // Controlled_Buffer controlled_buffer_2
  assign y2 = n2_4_decoder_1_out_5 ? x0 : 1'bz;  // Controlled_Buffer controlled_buffer_3
  assign y3 = n2_4_decoder_1_out_6 ? x0 : 1'bz;  // Controlled_Buffer controlled_buffer_4
  assign y0 = n2_4_decoder_1_out_4 ? x3 : 1'bz;  // Controlled_Buffer controlled_buffer_5
  assign y1 = n2_4_decoder_1_out_5 ? x3 : 1'bz;  // Controlled_Buffer controlled_buffer_6
  assign y2 = n2_4_decoder_1_out_6 ? x3 : 1'bz;  // Controlled_Buffer controlled_buffer_7
  assign y3 = n2_4_decoder_1_out_3 ? x3 : 1'bz;  // Controlled_Buffer controlled_buffer_8
  assign y0 = n2_4_decoder_1_out_5 ? x2 : 1'bz;  // Controlled_Buffer controlled_buffer_9
  assign y0 = n2_4_decoder_1_out_6 ? x1 : 1'bz;  // Controlled_Buffer controlled_buffer_10
  assign y1 = n2_4_decoder_1_out_3 ? x1 : 1'bz;  // Controlled_Buffer controlled_buffer_11
  assign y1 = n2_4_decoder_1_out_6 ? x2 : 1'bz;  // Controlled_Buffer controlled_buffer_12
  assign y2 = n2_4_decoder_1_out_4 ? x1 : 1'bz;  // Controlled_Buffer controlled_buffer_13
  assign y2 = n2_4_decoder_1_out_3 ? x2 : 1'bz;  // Controlled_Buffer controlled_buffer_14
  assign y3 = n2_4_decoder_1_out_5 ? x1 : 1'bz;  // Controlled_Buffer controlled_buffer_15
  assign y3 = n2_4_decoder_1_out_4 ? x2 : 1'bz;  // Controlled_Buffer controlled_buffer_16
endmodule

module _2_4_decoder (
  input  in_1,
  input  in_2,
  output out_3,
  output out_4,
  output out_5,
  output out_6
);

  wire not_1_out, not_2_out, not_3_out, not_4_out;

  not not_1 (not_1_out, in_1);
  not not_2 (not_2_out, in_2);
  not not_3 (not_3_out, in_1);
  not not_4 (not_4_out, in_2);
  and and_1 (out_3, not_1_out, not_2_out);
  and and_2 (out_4, not_3_out, in_2);
  and and_3 (out_5, in_1, not_4_out);
  and and_4 (out_6, in_1, in_2);
endmodule
