// Logisim project barrel_shift.circ as structural Verilog: 3 circuits, main circuit main
module main (
  input  in_1,
  input  in_2,
  input  in_3,
  input  in_4,
  input  [1:0] in_5,
  output out_6,
  output out_7,
  output out_8,
  output out_9
);

  Multiplexer #(.select(2)) multiplexer_1 (
    .in0(in_1), .in1(in_4), .in2(in_3), .in3(in_2), .out(out_6), .sel(in_5));  // open: en
  Multiplexer #(.select(2)) multiplexer_2 (
    .in0(in_2), .in1(in_1), .in2(in_4), .in3(in_3), .out(out_7), .sel(in_5));  // open: en
  Multiplexer #(.select(2)) multiplexer_3 (
    .in0(in_3), .in1(in_2), .in2(in_1), .in3(in_4), .out(out_8), .sel(in_5));  // open: en
  Multiplexer #(.select(2)) multiplexer_4 (
    .in0(in_4), .in1(in_3), .in2(in_2), .in3(in_1), .out(out_9), .sel(in_5));  // open: en
endmodule

module ex5 (
  input  A,
  input  B,
  input  [1:0] in_3,
  output out_4
);

  wire and_1_out, not_1_out, or_1_out, xor_1_out;

  and and_1 (and_1_out, A, B);
  xor xor_1 (xor_1_out, A, B);
  or or_1 (or_1_out, A, B);
  not not_1 (not_1_out, A);
  Multiplexer #(.select(2)) multiplexer_1 (
    .in0(and_1_out), .in1(xor_1_out), .in2(or_1_out), .in3(not_1_out), .out(out_4), .sel(in_3));  // open: en
endmodule

module exercise_5 (
  input  in_1,
  input  in_2,
  input  in_3,
  input  in_4,
  input  in_5,
  input  in_6,
  input  in_7,
  input  in_8,
  input  in_9,
  input  in_10,
  input  in_11,
  input  in_12,
  input  in_13,
  input  in_14,
  input  in_15,
  input  in_16,
  input  [1:0] in_17,
  output out_18,
  output out_19,
  output out_20,
  output out_21,
  output out_22,
  output out_23,
  output out_24,
  output out_25
);

  ex5 ex5_1 (.A(in_2), .B(in_1), .in_3(in_17), .out_4(out_18));
  ex5 ex5_2 (.A(in_4), .B(in_3), .in_3(in_17), .out_4(out_19));
  ex5 ex5_3 (.A(in_6), .B(in_5), .in_3(in_17), .out_4(out_20));
  ex5 ex5_4 (.A(in_8), .B(in_7), .in_3(in_17), .out_4(out_21));
  ex5 ex5_5 (.A(in_10), .B(in_9), .in_3(in_17), .out_4(out_22));
  ex5 ex5_6 (.A(in_12), .B(in_11), .in_3(in_17), .out_4(out_23));
  ex5 ex5_7 (.A(in_14), .B(in_13), .in_3(in_17), .out_4(out_24));
  ex5 ex5_8 (.A(in_16), .B(in_15), .in_3(in_17), .out_4(out_25));
endmodule
